// Digital circuit control_bomba.dig as structural Verilog
module control_bomba (
  input  tanqueH,
  input  tanqueL,
  input  cisternaOK,
  input  cisternaL,
  output bomba
);

  wire and_1_out, nand_1_out;

  nand nand_1 (nand_1_out, tanqueH, tanqueL);
  and and_1 (and_1_out, cisternaOK, cisternaL);
  and and_2 (bomba, nand_1_out, and_1_out);
endmodule
